// Logisim project 2018_04_26_lastone.circ as structural Verilog: 1 circuit, main circuit main
module main (
  input  [3:0] in_1,
  input  in_2,
  input  in_3,
  input  in_4,
  input  [1:0] in_5,
  input  [1:0] in_6,
  output out_7,
  output out_8,
  output [3:0] out_9
);

  wire clock_1_out, clock_2_out, clock_3_out, clock_4_out, clock_5_out, demultiplexer_1_out0,
       demultiplexer_1_out1, demultiplexer_1_out2, demultiplexer_1_out3, n4_bit_register_3_p5, nand_1_out,
       nand_2_out, nand_3_out, nand_4_out, not_1_out;
  wire [3:0] n4_bit_register_1_p4, n4_bit_register_2_p4, n4_bit_register_3_p4;

  Clock clock_1 (.out(clock_1_out));
  not not_1 (not_1_out, clock_1_out);
  nand nand_1 (nand_1_out, nand_4_out, nand_2_out);
  nand nand_2 (nand_2_out, nand_1_out, not_1_out);
  nand nand_3 (nand_3_out, nand_2_out, not_1_out, nand_4_out);
  nand nand_4 (nand_4_out, nand_3_out, in_2);
  nand nand_5 (out_7, nand_2_out, out_8);
  nand nand_6 (out_8, out_7, nand_3_out);
  Demultiplexer #(.select(2)) demultiplexer_1 (
    .out0(demultiplexer_1_out0), .out1(demultiplexer_1_out1), .out2(demultiplexer_1_out2),
    .out3(demultiplexer_1_out3), .in(in_3), .sel(in_6), .en(in_4));
  Clock clock_2 (.out(clock_2_out));
  Clock clock_3 (.out(clock_3_out));
  Clock clock_4 (.out(clock_4_out));
  Clock clock_5 (.out(clock_5_out));
  // _4_bit_Register 4_bit_register_1: pin names not known; wires that end beside it: in_1, clock_2_out, demultiplexer_1_out0, n4_bit_register_1_p4
  // _4_bit_Register 4_bit_register_2: pin names not known; wires that end beside it: in_1, clock_3_out, demultiplexer_1_out1, n4_bit_register_2_p4
  // _4_bit_Register 4_bit_register_3: pin names not known; wires that end beside it: in_1, clock_4_out, demultiplexer_1_out2, n4_bit_register_3_p4, n4_bit_register_3_p5
  // _4_bit_Register 4_bit_register_4: pin names not known; wires that end beside it: in_1, clock_5_out, demultiplexer_1_out3, n4_bit_register_3_p5
  Multiplexer #(.select(2), .width(4), .enable("false")) multiplexer_1 (
    .in0(n4_bit_register_1_p4), .in1(n4_bit_register_2_p4), .in3(n4_bit_register_3_p4), .out(out_9),
    .sel(in_5));  // open: in2
endmodule
