// Logisim project 2018_4_26_.circ as structural Verilog: 1 circuit, main circuit main
module main (
  input  [3:0] in_1,
  input  in_2,
  input  in_3,
  input  [1:0] in_4,
  output [3:0] out_5,
  output [1:0] out_6
);

  wire clock_1_out, clock_2_out, clock_3_out, clock_4_out, demultiplexer_1_out0, demultiplexer_1_out1,
       demultiplexer_1_out2, demultiplexer_1_out3;
  wire [3:0] n4_bit_register_1_out_4, n4_bit_register_2_out_4, n4_bit_register_3_out_4,
       n4_bit_register_4_out_4;

  Demultiplexer #(.select(2)) demultiplexer_1 (
    .out0(demultiplexer_1_out0), .out1(demultiplexer_1_out1), .out2(demultiplexer_1_out2),
    .out3(demultiplexer_1_out3), .in(in_2), .sel(in_4), .en(in_3));
  Clock clock_1 (.out(clock_1_out));
  Clock clock_2 (.out(clock_2_out));
  Clock clock_3 (.out(clock_3_out));
  Clock clock_4 (.out(clock_4_out));
  _4_bit_Register u_4_bit_register_1 (
    .load(demultiplexer_1_out0), .clock(clock_1_out), .in_3(in_1), .out_4(n4_bit_register_1_out_4));
  _4_bit_Register u_4_bit_register_2 (
    .load(demultiplexer_1_out1), .clock(clock_2_out), .in_3(in_1), .out_4(n4_bit_register_2_out_4));
  _4_bit_Register u_4_bit_register_3 (
    .load(demultiplexer_1_out2), .clock(clock_3_out), .in_3(in_1), .out_4(n4_bit_register_3_out_4));
  _4_bit_Register u_4_bit_register_4 (
    .load(demultiplexer_1_out3), .clock(clock_4_out), .in_3(in_1), .out_4(n4_bit_register_4_out_4));
  Multiplexer #(.select(2), .width(4), .enable("false")) multiplexer_1 (
    .in0(n4_bit_register_1_out_4), .in1(n4_bit_register_2_out_4), .in2(n4_bit_register_3_out_4),
    .in3(n4_bit_register_4_out_4), .out(out_5), .sel(out_6));
endmodule
