// Logisim project 32bit register.circ as structural Verilog: 1 circuit, main circuit main
module main (
  input  [31:0] \input ,
  input  load,
  input  clock,
  output [31:0] \output 
);

  _4_bit_Register u_4_bit_register_1 (.load(load), .clock(clock), .in_3(\input [31:28]), .out_4(\output [31:28]));
  _4_bit_Register u_4_bit_register_2 (.load(load), .clock(clock), .in_3(\input [27:24]), .out_4(\output [27:24]));
  _4_bit_Register u_4_bit_register_3 (.load(load), .clock(clock), .in_3(\input [23:20]), .out_4(\output [23:20]));
  _4_bit_Register u_4_bit_register_4 (.load(load), .clock(clock), .in_3(\input [19:16]), .out_4(\output [19:16]));
  _4_bit_Register u_4_bit_register_5 (.load(load), .clock(clock), .in_3(\input [15:12]), .out_4(\output [15:12]));
  _4_bit_Register u_4_bit_register_6 (.load(load), .clock(clock), .in_3(\input [11:8]), .out_4(\output [11:8]));
  _4_bit_Register u_4_bit_register_7 (.load(load), .clock(clock), .in_3(\input [7:4]), .out_4(\output [7:4]));
  _4_bit_Register u_4_bit_register_8 (.load(load), .clock(clock), .in_3(\input [3:0]), .out_4(\output [3:0]));
endmodule
