// Logisim project Computer_Architecture1_Data_Path.circ as structural Verilog: 1 circuit, main circuit main
module main (
  input  Enable,
  input  Clear,
  output [7:0] out_3,
  output [31:0] out_4,
  output [31:0] out_5
);

  wire ALU_zero, and_1_out, clock_1_out, clock_2_out, clock_3_out, main_1_alu_source, main_1_branch,
       main_1_jump, main_1_memory_read, main_1_memory_to_register, main_1_memory_write, main_1_r_i,
       main_1_register_write;
  wire [3:0] main_1_alu_operater;
  wire [4:0] multiplexer_2_out;
  wire [7:0] PC_output, PC_output_2, PC_output_3, PC_output_4;
  wire [15:0] rom_1_data;
  wire [27:0] bit_extender_2_out, shifter_1_out;
  wire [31:0] adder_1_out, adder_2_out, bit_extender_1_out, main_2_out_8, multiplexer_1_out,
       multiplexer_3_out, multiplexer_4_out, ram_1_data, shifter_2_out;
  wire [31:8] ALU_out_5;
  wire [31:16] rom_1_data_2;

  _32bit_register_main PC (
    .\input (multiplexer_4_out), .load(1'b1), .clock(clock_1_out),
    .\output ({PC_output_4, PC_output_3, PC_output_2, PC_output}));
  Clock clock_1 (.out(clock_1_out));
  assign bit_extender_1_out = {{16{1'b0}}, rom_1_data};  // Bit_Extender bit_extender_1
  ROM #(.dataWidth(32)) rom_1 (.addr(PC_output), .data({rom_1_data_2, rom_1_data}), .sel(1'b1));
  Multiplexer #(.width(32), .enable("false")) multiplexer_1 (
    .in0(out_5), .in1(bit_extender_1_out), .out(multiplexer_1_out), .sel(main_1_alu_source));
  ALU_Control_main ALU (
    .A(main_2_out_8), .B(multiplexer_1_out), .Register(main_1_alu_operater), .Enable(1'b1),
    .out_5({ALU_out_5, out_3}), .Zero(ALU_zero));
  assign bit_extender_2_out = {{2{1'b0}}, {rom_1_data_2[25:16], rom_1_data}};  // Bit_Extender bit_extender_2
  Adder #(.width(32)) adder_1 (
    .a({PC_output_4, PC_output_3, PC_output_2, PC_output}), .b(32'h4), .out(adder_1_out));  // open: cin, cout
  Control_main main_1 (
    .Input(rom_1_data_2[31:26]), .Function(rom_1_data[5:0]), .ALU_Operater(main_1_alu_operater),
    .Register_Write(main_1_register_write), .ALU_Source(main_1_alu_source),
    .Memory_Write(main_1_memory_write), .Memory_Read(main_1_memory_read),
    .Memory_to_Register(main_1_memory_to_register), .Branch(main_1_branch), .Jump(main_1_jump),
    .R_I(main_1_r_i));
  Shifter #(.width(28)) shifter_1 (.in(bit_extender_2_out), .\dist (5'b00010), .out(shifter_1_out));
  Multiplexer #(.width(5), .enable("false")) multiplexer_2 (
    .in0(rom_1_data_2[20:16]), .in1(rom_1_data[15:11]), .out(multiplexer_2_out), .sel(main_1_r_i));
  Clock clock_2 (.out(clock_2_out));
  R_Format_Instructor_main main_2 (
    .rs(rom_1_data_2[25:21]), .Input(main_1_register_write), .Enable(Enable), .rt(rom_1_data_2[20:16]),
    .rd(multiplexer_2_out), .Input32(out_4), .Clock(clock_2_out), .out_8(main_2_out_8), .out_9(out_5));
  and and_1 (and_1_out, main_1_branch, ALU_zero);
  Adder #(.width(32)) adder_2 (.a(adder_1_out), .b(shifter_2_out), .out(adder_2_out));  // open: cin, cout
  Shifter #(.width(32)) shifter_2 (.in(bit_extender_1_out), .\dist (5'b00010), .out(shifter_2_out));
  Clock clock_3 (.out(clock_3_out));
  Multiplexer #(.width(32), .enable("false")) multiplexer_3 (
    .in0(adder_1_out), .in1(adder_2_out), .out(multiplexer_3_out), .sel(and_1_out));
  RAM #(.dataWidth(32), .bus("separate")) ram_1 (
    .addr(out_3), .din(out_5), .data(ram_1_data), .str(main_1_memory_write), .sel(1'b1), .clk(clock_3_out),
    .ld(main_1_memory_read), .clr(Clear));
  Multiplexer #(.width(32), .enable("false")) multiplexer_4 (
    .in0(multiplexer_3_out), .in1({adder_1_out[31:28], shifter_1_out}), .out(multiplexer_4_out),
    .sel(main_1_jump));
  Multiplexer #(.width(32), .enable("false")) multiplexer_5 (
    .in0({ALU_out_5, out_3}), .in1(ram_1_data), .out(out_4), .sel(main_1_memory_to_register));

  // Notes on the sheet:
  //   contents of rom_1 (hex, n*v repeats v):
  //   20110004 0 0 0 20120005 0 0 0 2329820 0 0 0 ae330004 0 0 0 8e340004 0 0 0 12930001 0 0 0 274a820
endmodule
