// Logisim project Control.circ as structural Verilog: 1 circuit, main circuit main
module main (
  input  [5:0] Input,
  input  [5:0] Function,
  output [3:0] ALU_Operater,
  output Register_Write,
  output ALU_Source,
  output Memory_Write,
  output Memory_Read,
  output Memory_to_Register,
  output Branch,
  output Jump,
  output R_I
);

  wire Add_out, Addi_out, And_2_out, or_2_out, Or_out, Slt_out, Sub_out;
  wire [3:0] controlled_buffer_1_out;

  and and_1 (R_I, ~Input[0], ~Input[1], ~Input[2], ~Input[3], ~Input[4], ~Input[5]);  // AND_Gate
  and Addi (Addi_out, ~Input[0], ~Input[1], ~Input[2], Input[3], ~Input[4], ~Input[5]);  // AND_Gate
  and Lw (Memory_Read, Input[0], Input[1], ~Input[2], ~Input[3], ~Input[4], Input[5]);  // AND_Gate
  and Sw (Memory_Write, Input[0], Input[1], ~Input[2], Input[3], ~Input[4], Input[5]);  // AND_Gate
  and Beq (Branch, ~Input[0], ~Input[1], ~Input[2], Input[3], ~Input[4], ~Input[5]);  // AND_Gate
  and u_Jump (Jump, ~Input[0], Input[1], ~Input[2], ~Input[3], ~Input[4], ~Input[5]);  // AND_Gate
  and Add (Add_out, ~Function[0], ~Function[1], ~Function[2], ~Function[3], ~Function[4], Function[5]);  // AND_Gate
  and Sub (Sub_out, ~Function[0], Function[1], ~Function[2], ~Function[3], ~Function[4], Function[5]);  // AND_Gate
  and And_2 (And_2_out, ~Function[0], ~Function[1], Function[2], ~Function[3], ~Function[4], Function[5]);  // AND_Gate
  and Or (Or_out, Function[0], ~Function[1], Function[2], ~Function[3], ~Function[4], Function[5]);  // AND_Gate
  and Slt (Slt_out, ~Function[0], Function[1], ~Function[2], Function[3], ~Function[4], Function[5]);  // AND_Gate
  assign controlled_buffer_1_out = Add_out ? 4'b0010 : 4'bz;  // Controlled_Buffer controlled_buffer_1
  assign controlled_buffer_1_out = Sub_out ? 4'b0110 : 4'bz;  // Controlled_Buffer controlled_buffer_2
  assign controlled_buffer_1_out = And_2_out ? 4'b0000 : 4'bz;  // Controlled_Buffer controlled_buffer_3
  assign controlled_buffer_1_out = Or_out ? 4'b0001 : 4'bz;  // Controlled_Buffer controlled_buffer_4
  Controlled_Buffer #(.width(4)) controlled_buffer_5 (.in(4'b1111), .en(Slt_out));  // open: out
  or or_2 (or_2_out, Memory_Read, Memory_Write, Addi_out, Branch, Jump);
  assign ALU_Operater = or_2_out ? 4'b0010 : 4'bz;  // Controlled_Buffer controlled_buffer_6
  or or_3 (Register_Write, R_I, Addi_out, Memory_Read);
  or or_4 (ALU_Source, Addi_out, Memory_Read, Memory_Write);
  assign ALU_Operater = R_I ? controlled_buffer_1_out : 4'bz;  // Controlled_Buffer controlled_buffer_7

  assign Memory_to_Register = Memory_Read;
endmodule
