// Logisim project Data_path.circ as structural Verilog: 1 circuit, main circuit main
module main (
  input  [4:0] in_1,
  input  [31:0] in_2,
  input  [4:0] in_3,
  input  Enable,
  input  R_I,
  input  in_6,
  input  Select,
  input  Clear,
  output [7:0] out_9,
  output [31:0] out_10,
  output [31:0] out_11
);

  wire ALU_zero, and_1_out, clock_1_out, clock_2_out, Control_p4, Control_p5, Control_p6, Control_p7,
       Control_p8, Control_p9, Control_p10;
  wire [3:0] Control_p3;
  wire [4:0] multiplexer_2_out;
  wire [7:0] PC_output, PC_output_2, PC_output_3, PC_output_4;
  wire [15:0] rom_1_data;
  wire [27:0] bit_extender_2_out, shifter_1_out;
  wire [31:0] adder_1_out, adder_2_out, bit_extender_1_out, multiplexer_1_out, multiplexer_3_out,
       multiplexer_4_out, ram_1_data, Registers_out_8, shifter_2_out;
  wire [31:8] ALU_out_5;
  wire [31:16] rom_1_data_2;

  _32bit_register_main PC (
    .\input (multiplexer_4_out), .load(1'b1), .clock(clock_1_out),
    .\output ({PC_output_4, PC_output_3, PC_output_2, PC_output}));
  Clock clock_1 (.out(clock_1_out));
  assign bit_extender_1_out = {{16{1'b0}}, rom_1_data};  // Bit_Extender bit_extender_1
  ROM #(.dataWidth(32)) rom_1 (.addr(PC_output), .data({rom_1_data_2, rom_1_data}), .sel(1'b1));
  Multiplexer #(.width(32), .enable("false")) multiplexer_1 (
    .in0(out_11), .in1(bit_extender_1_out), .out(multiplexer_1_out), .sel(Control_p5));
  ALU_Control_main ALU (
    .A(Registers_out_8), .B(multiplexer_1_out), .Register(Control_p3), .Enable(in_6),
    .out_5({ALU_out_5, out_9}), .Zero(ALU_zero));
  assign bit_extender_2_out = {{2{1'b0}}, {rom_1_data_2, rom_1_data[15:6]}};  // Bit_Extender bit_extender_2
  Adder #(.width(32)) adder_1 (
    .a({PC_output_4, PC_output_3, PC_output_2, PC_output}), .b(in_2), .out(adder_1_out));  // open: cin, cout
  // Control_main Control: pin names not known; wires that end beside it: rom_1_data_2[31:26], rom_1_data[5:0], Control_p3, Control_p4, Control_p5, Control_p6, Control_p7, Control_p8, Control_p9, Control_p10
  Shifter #(.width(28)) shifter_1 (.in(bit_extender_2_out), .\dist (in_1), .out(shifter_1_out));
  Clock clock_2 (.out(clock_2_out));
  Multiplexer #(.width(5), .enable("false")) multiplexer_2 (
    .in0(rom_1_data[15:11]), .in1(rom_1_data_2[20:16]), .out(multiplexer_2_out), .sel(R_I));
  R_Format_Instructor_main Registers (
    .rs(rom_1_data_2[25:21]), .Input(Control_p4), .Enable(Enable), .rt(rom_1_data_2[20:16]),
    .rd(multiplexer_2_out), .Input32(out_10), .Clock(clock_2_out), .out_8(Registers_out_8), .out_9(out_11));
  and and_1 (and_1_out, Control_p9, ALU_zero);
  Adder #(.width(32)) adder_2 (.a(adder_1_out), .b(shifter_2_out), .out(adder_2_out));  // open: cin, cout
  Shifter #(.width(32)) shifter_2 (.in(bit_extender_1_out), .\dist (in_3), .out(shifter_2_out));
  Multiplexer #(.width(32), .enable("false")) multiplexer_3 (
    .in0(adder_1_out), .in1(adder_2_out), .out(multiplexer_3_out), .sel(and_1_out));
  RAM #(.dataWidth(32), .bus("separate")) ram_1 (
    .addr(out_9), .din(out_11), .data(ram_1_data), .str(Control_p6), .sel(Select), .ld(Control_p7),
    .clr(Clear));  // open: clk
  Multiplexer #(.width(32), .enable("false")) multiplexer_4 (
    .in0({adder_1_out[31:28], shifter_1_out}), .in1(multiplexer_3_out), .out(multiplexer_4_out),
    .sel(Control_p10));
  Multiplexer #(.width(32), .enable("false")) multiplexer_5 (
    .in0(ram_1_data), .in1({ALU_out_5, out_9}), .out(out_10), .sel(Control_p8));

  // Notes on the sheet:
  //   contents of rom_1 (hex, n*v repeats v):
  //   20110003 0 0 0 20120005 0 0 0 2329820 0 0 0 8e680020 0 0 0 2484020
endmodule
