// Logisim project Instruction_Fetch.circ as structural Verilog: 1 circuit, main circuit main
module main (
  input  [7:0] in_1,
  input  in_2,
  input  in_3,
  output [31:0] out_4
);

  wire adder_1_cout, clock_1_out, undriven;
  wire [7:0] main_1_output, main_1_output_2, main_1_output_3, main_1_output_4;
  wire [31:0] adder_1_out;

  _32bit_register_main main_1 (
    .\input (adder_1_out), .load(in_2), .clock(clock_1_out),
    .\output ({main_1_output_4, main_1_output_3, main_1_output_2, main_1_output}));
  Clock clock_1 (.out(clock_1_out));
  ROM #(.dataWidth(32)) rom_1 (.addr(main_1_output), .data(out_4), .sel(in_3));
  Adder adder_1 (.a(main_1_output), .b(in_1), .out(adder_1_out[7:0]), .cin(undriven), .cout(adder_1_cout));
endmodule
