// Logisim project R-Format_Instructor.circ as structural Verilog: 1 circuit, main circuit main
module main (
  input  [4:0] rs,
  input  Input,
  input  Enable,
  input  [4:0] rt,
  input  [4:0] rd,
  input  [31:0] Input32,
  input  Clock,
  output [31:0] out_8,
  output [31:0] out_9
);

  wire demultiplexer_1_out0, demultiplexer_1_out1, demultiplexer_1_out2, demultiplexer_1_out3;
  wire [31:0] main_1_out_8, main_1_out_9, main_2_out_8, main_2_out_9, main_3_out_8, main_3_out_9,
       main_4_out_8, main_4_out_9;

  Demultiplexer #(.select(2)) demultiplexer_1 (
    .out0(demultiplexer_1_out0), .out1(demultiplexer_1_out1), .out2(demultiplexer_1_out2),
    .out3(demultiplexer_1_out3), .in(Input), .sel(rd[4:3]), .en(Enable));
  register_file1_main main_1 (
    .in_1(Input32), .muxselect1(rs[2:0]), .load(demultiplexer_1_out0), .muxselect2(rt[2:0]),
    .Demuxselect(rd[2:0]), .clock(Clock), .out_8(main_1_out_8), .out_9(main_1_out_9));  // open: input2
  register_file1_main main_2 (
    .in_1(Input32), .muxselect1(rs[2:0]), .load(demultiplexer_1_out1), .muxselect2(rt[2:0]),
    .Demuxselect(rd[2:0]), .clock(Clock), .out_8(main_2_out_8), .out_9(main_2_out_9));  // open: input2
  register_file1_main main_3 (
    .in_1(Input32), .muxselect1(rs[2:0]), .load(demultiplexer_1_out2), .muxselect2(rt[2:0]),
    .Demuxselect(rd[2:0]), .clock(Clock), .out_8(main_3_out_8), .out_9(main_3_out_9));  // open: input2
  register_file1_main main_4 (
    .in_1(Input32), .muxselect1(rs[2:0]), .load(demultiplexer_1_out3), .muxselect2(rt[2:0]),
    .Demuxselect(rd[2:0]), .clock(Clock), .out_8(main_4_out_8), .out_9(main_4_out_9));  // open: input2
  Multiplexer #(.select(2), .width(32), .enable("false")) multiplexer_1 (
    .in0(main_1_out_8), .in1(main_2_out_8), .in2(main_3_out_8), .in3(main_4_out_8), .out(out_8), .sel(rs[4:3]));
  Multiplexer #(.select(2), .width(32), .enable("false")) multiplexer_2 (
    .in0(main_1_out_9), .in1(main_2_out_9), .in2(main_3_out_9), .in3(main_4_out_9), .out(out_9), .sel(rt[4:3]));
endmodule
