// Logisim project Ripple Carry Adder.circ as structural Verilog: 1 circuit, main circuit main
module main (
  input  in_1,
  input  in_2,
  input  in_3,
  input  in_4,
  input  in_5,
  input  in_6,
  input  in_7,
  input  in_8,
  input  in_9,
  input  in_10,
  input  in_11,
  output out_12
);

  wire full_adder_1_cout, full_adder_2_cout, full_adder_3_cout, full_adder_4_cout;

  Full_Adder full_adder_1 (.x(in_1), .y(in_2), .cin(in_3), .cout(full_adder_1_cout));  // open: sum
  Full_Adder full_adder_2 (.x(in_4), .y(in_5), .cin(full_adder_1_cout), .cout(full_adder_2_cout));  // open: sum
  Full_Adder full_adder_3 (.x(in_6), .y(in_7), .cin(full_adder_2_cout), .cout(full_adder_3_cout));  // open: sum
  Full_Adder full_adder_4 (.x(in_8), .y(in_9), .cin(full_adder_3_cout), .cout(full_adder_4_cout));  // open: sum
  Full_Adder full_adder_5 (.x(in_10), .y(in_11), .cin(full_adder_4_cout));  // open: sum, cout
  xor xor_1 (out_12, full_adder_3_cout, full_adder_4_cout);
endmodule
