// Logisim project combinational.circ as structural Verilog: 8 circuits, main circuit Half Adder
module Half_Adder (
  input  x,
  input  y,
  output sum,
  output carry
);

  xor xor_1 (sum, x, y);
  and and_1 (carry, x, y);
endmodule

module Full_Adder (
  input  x,
  input  y,
  input  cin,
  output sum,
  output cout
);

  wire half_adder_1_carry, half_adder_1_sum, half_adder_2_carry;

  Half_Adder half_adder_1 (.sum(half_adder_1_sum), .carry(half_adder_1_carry), .x(x), .y(y));
  Half_Adder half_adder_2 (.sum(sum), .carry(half_adder_2_carry), .x(half_adder_1_sum), .y(cin));
  or or_1 (cout, half_adder_2_carry, half_adder_1_carry);
endmodule

module _4_bit_Ripple_Carry_Adder (
  input  cin,
  input  [3:0] x,
  input  [3:0] y,
  output [3:0] sum,
  output Overflow,
  output cout
);

  wire full_adder_1_cout, full_adder_2_cout, full_adder_3_cout;

  Full_Adder full_adder_1 (.x(x[0]), .y(y[0]), .cin(cin), .sum(sum[0]), .cout(full_adder_1_cout));
  Full_Adder full_adder_2 (.x(x[1]), .y(y[1]), .cin(full_adder_1_cout), .sum(sum[1]), .cout(full_adder_2_cout));
  Full_Adder full_adder_3 (.x(x[2]), .y(y[2]), .cin(full_adder_2_cout), .sum(sum[2]), .cout(full_adder_3_cout));
  Full_Adder full_adder_4 (.x(x[3]), .y(y[3]), .cin(full_adder_3_cout), .sum(sum[3]), .cout(cout));
  xor xor_1 (Overflow, full_adder_3_cout, cout);
endmodule

module _2_to_4_Decoder (
  input  enable,
  input  [1:0] a1_a0,
  output d0,
  output d1,
  output d2,
  output d3
);

  Decoder #(.select(2)) decoder_1 (.out0(d0), .out1(d1), .out2(d2), .out3(d3), .sel(a1_a0), .en(enable));
endmodule

module _3_to_8_Decoder (
  input  a0,
  input  a1,
  input  a2,
  output d0,
  output d1,
  output d2,
  output d3,
  output d0_2,
  output d1_2,
  output d2_2,
  output d3_2
);

  wire not_1_out;

  Decoder #(.select(2)) decoder_1 (.out0(d0), .out1(d1), .out2(d2), .out3(d3), .sel({a1, a0}), .en(not_1_out));
  not not_1 (not_1_out, a2);
  Decoder #(.select(2)) decoder_2 (.out0(d0_2), .out1(d1_2), .out2(d2_2), .out3(d3_2), .sel({a1, a0}), .en(a2));
endmodule

module _4_to_1_MUX (
  input  d0,
  input  d1,
  input  d2,
  input  d3,
  input  [1:0] s1_s0,
  output f
);

  Multiplexer #(.select(2), .enable("false")) multiplexer_1 (
    .in0(d0), .in1(d1), .in2(d2), .in3(d3), .out(f), .sel(s1_s0));
endmodule

module _4_bit_Shifter (
  input  [3:0] in_1,
  input  Rin,
  input  Lin,
  input  [1:0] s1_s0,
  output [3:0] out_5
);

  Multiplexer #(.select(2), .enable("false")) multiplexer_1 (
    .in0(in_1[3]), .in1(Rin), .in2(in_1[2]), .in3(in_1[3]), .out(out_5[3]), .sel(s1_s0));
  Multiplexer #(.select(2), .enable("false")) multiplexer_2 (
    .in0(in_1[2]), .in1(in_1[3]), .in2(in_1[1]), .in3(in_1[2]), .out(out_5[2]), .sel(s1_s0));
  Multiplexer #(.select(2), .enable("false")) multiplexer_3 (
    .in0(in_1[1]), .in1(in_1[2]), .in2(in_1[0]), .in3(in_1[1]), .out(out_5[1]), .sel(s1_s0));
  Multiplexer #(.select(2), .enable("false")) multiplexer_4 (
    .in0(in_1[0]), .in1(in_1[1]), .in2(Lin), .in3(in_1[0]), .out(out_5[0]), .sel(s1_s0));
endmodule

module _4_bit_Arithmetic_Unit (
  input  [3:0] A,
  input  [3:0] B,
  input  [1:0] s1_s0,
  input  Cin,
  output [3:0] out_5,
  output Overflow,
  output Cout
);

  wire [3:0] multiplexer_1_out, not_1_out;

  assign not_1_out = ~B;  // NOT_Gate not_1, 4 bits wide
  Multiplexer #(.select(2), .width(4), .enable("false")) multiplexer_1 (
    .in0(4'b0000), .in1(B), .in2(not_1_out), .in3(4'b1111), .out(multiplexer_1_out), .sel(s1_s0));
  _4_bit_Ripple_Carry_Adder u_4_bit_ripple_carry_adder_1 (
    .cin(Cin), .x(A), .y(multiplexer_1_out), .sum(out_5), .Overflow(Overflow), .cout(Cout));
endmodule
