// Logisim project d-flipflop.circ as structural Verilog: 1 circuit, main circuit main
module main (
  input  in_1,
  output out_2,
  output out_3
);

  wire and_1_out, and_2_out, and_3_out, and_4_out, clock_1_out, nor_1_out, nor_2_out, not_1_out, not_2_out,
       not_3_out;

  Clock clock_1 (.out(clock_1_out));
  not not_1 (not_1_out, clock_1_out);
  not not_2 (not_2_out, in_1);
  and and_1 (and_1_out, in_1, not_1_out);
  and and_2 (and_2_out, not_1_out, not_2_out);
  nor nor_1 (nor_1_out, and_2_out, nor_2_out);
  nor nor_2 (nor_2_out, nor_1_out, and_1_out);
  and and_3 (and_3_out, nor_1_out, clock_1_out);
  and and_4 (and_4_out, clock_1_out, not_3_out);
  not not_3 (not_3_out, nor_1_out);
  nor nor_3 (out_2, and_4_out, out_3);
  nor nor_4 (out_3, out_2, and_3_out);
endmodule
