// Logisim project d-latch.circ as structural Verilog: 1 circuit, main circuit main
module main (
  input  in_1,
  input  in_2,
  output out_3,
  output out_4
);

  wire and_1_out, and_2_out, not_1_out;

  not not_1 (not_1_out, in_1);
  and and_1 (and_1_out, in_1, in_2);
  and and_2 (and_2_out, in_2, not_1_out);
  SR_Latch sr_latch_1 (.S(and_1_out), .R(and_2_out), .Q(out_3), .Q_prime(out_4));
endmodule
