// Logisim project logging.circ as structural Verilog: 1 circuit, main circuit main
module main (
  input  in_1,
  output out_2,
  output out_3
);

  wire clock_1_out;

  Clock clock_1 (.out(clock_1_out));
  D_Flipflop d_flipflop_1 (.D(in_1), .C(clock_1_out), .Q(out_2), .Q_prime(out_3));
endmodule
