// Logisim project register file.circ as structural Verilog: 1 circuit, main circuit main
module main (
  input  [31:0] in_1
);

  wire [31:0] demultiplexer_1_out0, demultiplexer_1_out1, demultiplexer_1_out2, demultiplexer_1_out3,
       demultiplexer_1_out4, demultiplexer_1_out5, demultiplexer_1_out6, demultiplexer_1_out7;

  Demultiplexer #(.select(3), .width(32)) demultiplexer_1 (
    .out0(demultiplexer_1_out0), .out1(demultiplexer_1_out1), .out2(demultiplexer_1_out2),
    .out3(demultiplexer_1_out3), .out4(demultiplexer_1_out4), .out5(demultiplexer_1_out5),
    .out6(demultiplexer_1_out6), .out7(demultiplexer_1_out7));  // open: in, sel, en
  // _32bit_register_main main_1: pin names not known; wires that end beside it: demultiplexer_1_out0, in_1
  // _32bit_register_main main_2: pin names not known; wires that end beside it: demultiplexer_1_out1, in_1
  // _32bit_register_main main_3: pin names not known; wires that end beside it: demultiplexer_1_out2, in_1
  // _32bit_register_main main_4: pin names not known; wires that end beside it: demultiplexer_1_out3, in_1
  // _32bit_register_main main_5: pin names not known; wires that end beside it: demultiplexer_1_out4, in_1
  // _32bit_register_main main_6: pin names not known; wires that end beside it: demultiplexer_1_out5, in_1
  // _32bit_register_main main_7: pin names not known; wires that end beside it: demultiplexer_1_out6, in_1
  // _32bit_register_main main_8: pin names not known; wires that end beside it: demultiplexer_1_out7, in_1
endmodule
