// Logisim project register file1.circ as structural Verilog: 1 circuit, main circuit main
module main (
  input  [31:0] in_1,
  input  [2:0] muxselect1,
  input  load,
  input  input2,
  input  [2:0] muxselect2,
  input  [2:0] Demuxselect,
  input  clock,
  output [31:0] out_8,
  output [31:0] out_9
);

  wire demultiplexer_1_out0, demultiplexer_1_out1, demultiplexer_1_out2, demultiplexer_1_out3,
       demultiplexer_1_out4, demultiplexer_1_out5, demultiplexer_1_out6, demultiplexer_1_out7;
  wire [31:0] main_1_output, main_2_output, main_3_output, main_4_output, main_5_output, main_6_output,
       main_7_output, main_8_output;

  Demultiplexer #(.select(3)) demultiplexer_1 (
    .out0(demultiplexer_1_out0), .out1(demultiplexer_1_out1), .out2(demultiplexer_1_out2),
    .out3(demultiplexer_1_out3), .out4(demultiplexer_1_out4), .out5(demultiplexer_1_out5),
    .out6(demultiplexer_1_out6), .out7(demultiplexer_1_out7), .in(load), .sel(Demuxselect), .en(input2));
  _32bit_register_main main_1 (.\input (in_1), .load(demultiplexer_1_out0), .clock(clock), .\output (main_1_output));
  _32bit_register_main main_2 (.\input (in_1), .load(demultiplexer_1_out1), .clock(clock), .\output (main_2_output));
  _32bit_register_main main_3 (.\input (in_1), .load(demultiplexer_1_out2), .clock(clock), .\output (main_3_output));
  _32bit_register_main main_4 (.\input (in_1), .load(demultiplexer_1_out3), .clock(clock), .\output (main_4_output));
  _32bit_register_main main_5 (.\input (in_1), .load(demultiplexer_1_out4), .clock(clock), .\output (main_5_output));
  _32bit_register_main main_6 (.\input (in_1), .load(demultiplexer_1_out5), .clock(clock), .\output (main_6_output));
  _32bit_register_main main_7 (.\input (in_1), .load(demultiplexer_1_out6), .clock(clock), .\output (main_7_output));
  _32bit_register_main main_8 (.\input (in_1), .load(demultiplexer_1_out7), .clock(clock), .\output (main_8_output));
  Multiplexer #(.select(3), .width(32), .enable("false")) multiplexer_1 (
    .in0(main_1_output), .in1(main_2_output), .in2(main_3_output), .in3(main_4_output), .in4(main_5_output),
    .in5(main_6_output), .in6(main_7_output), .in7(main_8_output), .out(out_8), .sel(muxselect1));
  Multiplexer #(.select(3), .width(32), .enable("false")) multiplexer_2 (
    .in0(main_1_output), .in1(main_2_output), .in2(main_3_output), .in3(main_4_output), .in4(main_5_output),
    .in5(main_6_output), .in6(main_7_output), .in7(main_8_output), .out(out_9), .sel(muxselect2));
endmodule
