// Logisim project sequential.circ as structural Verilog: 10 circuits, main circuit SR-Latch
module Half_Adder (
  input  x,
  input  y,
  output sum,
  output carry
);

  xor xor_1 (sum, x, y);
  and and_1 (carry, x, y);
endmodule

module SR_Latch (
  input  S,
  input  R,
  output Q,
  output Q_prime
);

  nor nor_1 (Q, R, Q_prime);
  nor nor_2 (Q_prime, Q, S);
endmodule

module D_Latch (
  input  D,
  input  C,
  output Q,
  output Q_prime
);

  wire and_1_out, and_2_out, not_1_out;

  not not_1 (not_1_out, D);
  and and_1 (and_1_out, D, C);
  and and_2 (and_2_out, C, not_1_out);
  SR_Latch sr_latch_1 (.S(and_1_out), .R(and_2_out), .Q(Q), .Q_prime(Q_prime));
endmodule

module D_Flipflop (
  input  D,
  input  C,
  output Q,
  output Q_prime
);

  wire d_latch_1_q, not_1_out;

  not not_1 (not_1_out, C);
  D_Latch d_latch_1 (.D(D), .Q(d_latch_1_q), .C(not_1_out));  // open: Q_prime
  D_Latch d_latch_2 (.D(d_latch_1_q), .Q(Q), .Q_prime(Q_prime), .C(C));
endmodule

module Clock___D_Flipflop (
  input  D,
  output Q,
  output Q_prime
);

  wire clock_1_out;

  Clock clock_1 (.out(clock_1_out));
  D_Flipflop d_flipflop_1 (.D(D), .C(clock_1_out), .Q(Q), .Q_prime(Q_prime));
endmodule

module _1_bit_Register (
  input  C,
  input  DI,
  input  load,
  output DO
);

  wire multiplexer_1_out;

  Multiplexer #(.enable("false")) multiplexer_1 (.in0(DO), .in1(DI), .out(multiplexer_1_out), .sel(load));
  D_Flip_Flop d_ff_1 (.clk(C), .D(multiplexer_1_out), .Q(DO));  // open: Qn, preset, en, reset
endmodule

module _4_bit_Register (
  input  load,
  input  clock,
  input  [3:0] in_3,
  output [3:0] out_4
);

  _1_bit_Register u_1_bit_register_1 (.DI(in_3[0]), .DO(out_4[0]), .load(load), .C(clock));
  _1_bit_Register u_1_bit_register_2 (.DI(in_3[1]), .DO(out_4[1]), .load(load), .C(clock));
  _1_bit_Register u_1_bit_register_3 (.DI(in_3[2]), .DO(out_4[2]), .load(load), .C(clock));
  _1_bit_Register u_1_bit_register_4 (.DI(in_3[3]), .DO(out_4[3]), .load(load), .C(clock));
endmodule

module Clock___4_bit_Register (
  input  in_1,
  input  [3:0] in_2,
  output [3:0] out_3
);

  wire clock_1_out;

  Clock clock_1 (.out(clock_1_out));
  _4_bit_Register u_4_bit_register_1 (.load(in_1), .clock(clock_1_out), .in_3(in_2), .out_4(out_3));
endmodule

module _4_bit_Counter (
  input  [3:0] in_1,
  input  inc,
  input  load,
  output carry,
  output [3:0] out_5
);

  wire clock_1_out, half_adder_1_sum, half_adder_2_carry, half_adder_2_sum, half_adder_3_carry,
       half_adder_3_sum, half_adder_4_carry, half_adder_4_sum, multiplexer_1_out, multiplexer_2_out,
       multiplexer_3_out, multiplexer_4_out;

  Clock clock_1 (.out(clock_1_out));
  Half_Adder half_adder_1 (.x(half_adder_2_carry), .y(out_5[3]), .sum(half_adder_1_sum), .carry(carry));
  Multiplexer #(.enable("false")) multiplexer_1 (
    .in0(half_adder_1_sum), .in1(in_1[3]), .out(multiplexer_1_out), .sel(load));
  D_Flip_Flop d_ff_1 (.clk(clock_1_out), .D(multiplexer_1_out), .Q(out_5[3]));  // open: Qn, preset, en, reset
  Half_Adder half_adder_2 (.x(half_adder_3_carry), .y(out_5[2]), .sum(half_adder_2_sum), .carry(half_adder_2_carry));
  Multiplexer #(.enable("false")) multiplexer_2 (
    .in0(half_adder_2_sum), .in1(in_1[2]), .out(multiplexer_2_out), .sel(load));
  D_Flip_Flop d_ff_2 (.clk(clock_1_out), .D(multiplexer_2_out), .Q(out_5[2]));  // open: Qn, preset, en, reset
  Half_Adder half_adder_3 (.x(half_adder_4_carry), .y(out_5[1]), .sum(half_adder_3_sum), .carry(half_adder_3_carry));
  Multiplexer #(.enable("false")) multiplexer_3 (
    .in0(half_adder_3_sum), .in1(in_1[1]), .out(multiplexer_3_out), .sel(load));
  D_Flip_Flop d_ff_3 (.clk(clock_1_out), .D(multiplexer_3_out), .Q(out_5[1]));  // open: Qn, preset, en, reset
  Half_Adder half_adder_4 (.x(inc), .y(out_5[0]), .sum(half_adder_4_sum), .carry(half_adder_4_carry));
  Multiplexer #(.enable("false")) multiplexer_4 (
    .in0(half_adder_4_sum), .in1(in_1[0]), .out(multiplexer_4_out), .sel(load));
  D_Flip_Flop d_ff_4 (.clk(clock_1_out), .D(multiplexer_4_out), .Q(out_5[0]));  // open: Qn, preset, en, reset
endmodule

module Memory (
  input  [3:0] Address,
  input  [7:0] DATAin,
  input  write,
  input  clock,
  output [7:0] DATAout
);

  wire not_1_out;

  not not_1 (not_1_out, write);
  RAM #(.addrWidth(4), .bus("separate")) ram_1 (
    .addr(Address), .din(DATAin), .data(DATAout), .str(write), .clk(clock), .ld(not_1_out));  // open: sel, clr
endmodule
